// Digital circuit UTS12.1.dig as structural Verilog
module UTS12_1 (
  input  X,
  input  Y,
  input  Z,
  output P
);

  wire and_1_out, and_2_out, and_3_out, not_1_out, not_2_out;

  not not_1 (not_1_out, Y);
  not not_2 (not_2_out, Z);
  and and_1 (and_1_out, X, Y, not_2_out);
  and and_2 (and_2_out, X, Z);
  and and_3 (and_3_out, not_1_out, not_2_out);
  or or_1 (P, and_1_out, and_2_out, and_3_out);
endmodule
