// Digital circuit UTS2.1.dig as structural Verilog
module UTS2_1 (
  input  A,
  input  B,
  input  C,
  input  D,
  output X
);

  wire and_2_out, and_3_out, and_4_out, and_5_out, and_6_out, not_1_out, not_2_out, not_3_out, not_4_out;

  not not_1 (not_1_out, A);
  not not_2 (not_2_out, B);
  not not_3 (not_3_out, C);
  not not_4 (not_4_out, C);
  // And and_1 has open pins: In_1=not_1_out, In_2=not_2_out, In_3=not_3_out, out=open
  and and_2 (and_2_out, not_1_out, C, C);
  and and_3 (and_3_out, not_1_out, not_3_out, not_4_out);
  and and_4 (and_4_out, not_1_out, B, C);
  and and_5 (and_5_out, A, B, C);
  and and_6 (and_6_out, A, not_2_out, C);
  or or_1 (X, and_6_out, and_4_out, C, and_2_out, and_5_out, and_3_out);

  assign D = C;

  // Notes on the sheet:
  //   SERLI SEPTIANI
endmodule
