// Digital circuit UTS3.1.dig as structural Verilog
module UTS3_1 (
  input  X,
  input  Y,
  input  Z,
  output S
);

  wire and_1_out, and_2_out, not_3_out;

  // Not not_1 has open pins: in=X, out=open
  // Not not_2 has open pins: in=Y, out=open
  not not_3 (not_3_out, Z);
  and and_1 (and_1_out, X, Y);
  and and_2 (and_2_out, Y, not_3_out);
  or or_1 (S, and_1_out, and_2_out);

  // Notes on the sheet:
  //   SERLI SEPTIANI
endmodule
