// Digital circuit UTS5.1.dig as structural Verilog
module UTS5_1 (
  input  A,
  input  B,
  input  C,
  input  D,
  output out_5
);

  wire and_1_out, and_2_out, and_3_out, and_4_out, not_1_out, not_2_out;

  not not_1 (not_1_out, A);
  not not_2 (not_2_out, B);
  not not_3 (not_2_out, C);
  not not_4 (not_2_out, D);
  and and_1 (and_1_out, B, C, D);
  and and_2 (and_2_out, not_1_out, not_2_out);
  and and_3 (and_3_out, not_1_out, not_2_out, not_2_out);
  and and_4 (and_4_out, not_2_out, not_2_out, not_2_out);
  or or_1 (out_5, and_3_out, and_1_out, and_4_out, and_2_out);
endmodule
