// Digital circuit UTS8.1.dig as structural Verilog
module UTS8_1 (
  input  A,
  input  B,
  input  C,
  input  D,
  output S
);

  wire and_1_out, and_2_out, and_3_out, and_4_out, and_5_out, not_1_out, not_2_out, not_3_out;

  not not_1 (not_1_out, A);
  not not_2 (not_2_out, C);
  not not_3 (not_3_out, B);
  and and_1 (and_1_out, not_1_out, B, not_3_out);
  and and_2 (and_2_out, B, C, B);
  and and_3 (and_3_out, A, B, not_2_out);
  and and_4 (and_4_out, A, B, C);
  and and_5 (and_5_out, B, B);
  or or_1 (S, and_1_out, and_4_out, and_5_out, and_2_out, and_3_out);

  assign D = B;
endmodule
