// Digital circuit praktikum5_2.dig as structural Verilog
module praktikum5_2 (
  input  A,
  input  B,
  output S
);

  wire not_1_out, not_2_out, or_1_out, or_2_out, or_3_out;

  not not_1 (not_1_out, A);
  not not_2 (not_2_out, B);
  or or_1 (or_1_out, B, B);
  or or_2 (or_2_out, A, not_2_out);
  or or_3 (or_3_out, not_1_out, B);
  and and_1 (S, or_1_out, or_2_out, or_3_out);
endmodule
