// Digital circuit serli s.dig as structural Verilog
module serli_s (
  input  CL,
  input  A
);

  wire nand_1_out, nor_1_out;

  nand nand_1 (nand_1_out, CL, A);
  nor nor_1 (nor_1_out, CL, A);
  LED led_1 (.in(nand_1_out));
  LED LED_2 (.in(nand_1_out));
  LED led_3 (.in(nor_1_out));
  LED led_4 (.in(nor_1_out));

  // Notes on the sheet:
  //   CL: Hz: 25
endmodule
